# Fritzing sketch circuit (saved by Fritzing 0.9.3b)
breadboards: 1

parts:
  U1 = ESP8266 NodeMCU LoLin module
  Part1 = Arduino Uno (Rev3)
  LED1 = LED - 5mm [color="Green (555nm)" package="5 mm [THT]"]
  LED2 = LED - 5mm [color="Green (555nm)" package="5 mm [THT]"]
  R1 = Resistor [tolerance=±5% resistance=220 package=THT]
  Part2 = SRF05 Ultrasonic Rangefinder
  R2 = Resistor [tolerance=±5% resistance=220 package=THT]
  BT1 = Bluetooth HC-06u [package=THT]
  J1 = Basic Servo
  T1 = LM35 Temperature Sensor [package="TO92 [THT]"]

nets:
  N1: U1.D2, LED1.anode
  N2: U1.D6, Part2.Trig
  N3: U1.D7, Part2.Echo
  N4: U1.VU, Part2.VCC
  N5: U1.A0, T1.Vout
  N6: Part1.D8, BT1.TXD
  N7: Part1.D9_PWM, BT1.RXD
  N8: Part1.D11_PWM/MOSI, J1.pulse
  N9: Part1.D4, LED2.anode
  VCC: Part1.5V, BT1.VCC, J1.vcc, T1.+Vs
  GND: Part1.GND, R1.Pin_0, Part2.GND, R2.Pin_0, BT1.GND, J1.gnd, T1.GND
  N10: LED1.cathode, R1.Pin_1
  N11: LED2.cathode, R2.Pin_1

custom parts:
  ESP8266 NodeMCU LoLin module: ESP8266 based NodeMCU
  Bluetooth HC-06u: Bluetooth HC-06 - face up, pins down 16.5mm x 37.5mm PCB
